// Logisim project add.circ as structural Verilog: 1 circuit, main circuit add
module add (
  input  [8:0] opand1,
  input  [8:0] opand2,
  output [8:0] result
);

  assign result = opand1 ^ opand2;  // XOR_Gate xor_1, 9 bits wide
endmodule
