// Logisim project alu.circ as structural Verilog: 1 circuit, main circuit alu
module alu (
  input  [8:0] opand1,
  input  [8:0] opand2,
  input  [8:0] size,
  input  enable,
  input  [1:0] opcode,
  output [8:0] result
);

  wire [8:0] add_1_result, div_1_result, log_1_result, mul_1_result;

  add add_1 (.opand1(opand1), .opand2(opand2), .result(add_1_result));
  mul mul_1 (.opand1(opand1), .opand2(opand2), .size(size), .result(mul_1_result));
  div div_1 (.opand1(opand1), .opand2(opand2), .size(size), .result(div_1_result));
  log log_1 (.opand1(opand1), .result(log_1_result));
  Multiplexer #(.select(2), .width(9)) multiplexer_1 (
    .in0(add_1_result), .in1(mul_1_result), .in2(div_1_result), .in3(log_1_result), .out(result),
    .sel(opcode), .en(enable));
endmodule
