// Logisim project cpu.circ as structural Verilog: 1 circuit, main circuit main
module main (
  output [5:0] out_1
);

  wire clock_1_out, comparator_1_eq, counter_1_q, counter_2_q, nand_1_out, not_1_out, not_2_out, not_3_out,
       reset_out;
  wire [5:0] adder_1_out, demultiplexer_1_out0, demultiplexer_1_out1, multiplexer_1_out, multiplexer_2_out,
       multiplexer_3_out, opand1_q, opand2_q, PC_q, rom_1_data;
  wire [15:0] ram_1_dout;

  Clock clock_1 (.out(clock_1_out));
  Button reset (.out(reset_out));
  Counter #(.max('h1), .width(1)) counter_1 (
    .count(clock_1_out), .Q(counter_1_q), .up(1'b1), .clk(clock_1_out), .clr(reset_out));  // open: load, D, carry
  Adder #(.width(6)) adder_1 (.a(PC_q), .b(6'b000001), .out(adder_1_out));  // open: cin, cout
  Register #(.width(6)) PC (.D(adder_1_out), .en(1'b1), .clk(not_1_out), .Q(PC_q), .clr(reset_out));
  not not_1 (not_1_out, counter_1_q);
  Comparator #(.mode("unsigned"), .width(1)) comparator_1 (
    .a(counter_1_q), .b(1'b1), .eq(comparator_1_eq));  // open: gt, lt
  not not_2 (not_2_out, comparator_1_eq);
  RAM #(.addrWidth(6), .dataWidth(16)) ram_1 (
    .addr(PC_q), .we(1'b0), .oe(1'b1), .clk(counter_1_q), .dout(ram_1_dout));  // open: din
  LED led_1 (.in(comparator_1_eq));
  nand nand_1 (nand_1_out, ram_1_dout[14], clock_1_out);
  Multiplexer #(.enable("false"), .width(6)) multiplexer_1 (
    .in0(ram_1_dout[5:0]), .in1(ram_1_dout[11:6]), .out(multiplexer_1_out), .sel(counter_2_q));
  Counter #(.max('h1), .width(1)) counter_2 (
    .count(nand_1_out), .Q(counter_2_q), .up(1'b1), .clk(nand_1_out));  // open: load, D, carry, clr
  ROM #(.addrWidth(6), .dataWidth(6)) rom_1 (.addr(multiplexer_1_out), .data(rom_1_data));
  Multiplexer #(.enable("false"), .width(6)) multiplexer_2 (
    .in0(ram_1_dout[5:0]), .in1(demultiplexer_1_out0), .out(multiplexer_2_out), .sel(ram_1_dout[14]));
  Register #(.trigger("high"), .width(6)) opand2 (
    .D(multiplexer_2_out), .en(clock_1_out), .clk(clock_1_out), .Q(opand2_q));  // open: clr
  Multiplexer #(.enable("false"), .width(6)) multiplexer_3 (
    .in0(ram_1_dout[11:6]), .in1(demultiplexer_1_out1), .out(multiplexer_3_out), .sel(ram_1_dout[14]));
  Register #(.trigger("high"), .width(6)) opand1 (
    .D(multiplexer_3_out), .en(not_3_out), .clk(not_3_out), .Q(opand1_q));  // open: clr
  not not_3 (not_3_out, clock_1_out);
  Demultiplexer #(.enable("false"), .width(6)) demultiplexer_1 (
    .out0(demultiplexer_1_out0), .out1(demultiplexer_1_out1), .in(rom_1_data), .sel(counter_2_q));
  alu alu_1 (.opand1(opand1_q), .opand2(opand2_q), .enable(not_2_out), .opcode(ram_1_dout[13:12]), .result(out_1));
  // also tied to GND on the sheet: ram_1_dout[15]

  // Notes on the sheet:
  //   logp 3: 0x30c0
  //   multp 4, 6: 0x1106
  //   contents of rom_1 (hex, n*v repeats v):
  //   1 2 4 5 7 3 6
endmodule
