// Logisim project cpu3.circ as structural Verilog: 4 circuits, main circuit main
module main (
  output [8:0] out_1
);

  wire clock_1_out, gen_1_ld, not_1_out, not_2_out, reset_out;
  wire [2:0] ram_1_dout_2;
  wire [8:0] alu_1_p6, demultiplexer_1_out0, demultiplexer_1_out1, gen_1_dout, gen_1_size, opand1_q,
       opand2_q, pc_1_line, ram_1_dout;

  Button reset (.out(reset_out));
  Clock clock_1 (.out(clock_1_out));
  pc pc_1 (.line(pc_1_line), .in_4(ram_1_dout_2), .size(gen_1_size), .clk(clock_1_out), .rst(reset_out));
  RAM #(.addrWidth(9), .dataWidth(12), .\type ("nonvolatile")) ram_1 (
    .addr(pc_1_line), .we(1'b0), .oe(1'b1), .clk(clock_1_out),
    .dout({ram_1_dout_2[0], ram_1_dout_2[2:1], ram_1_dout}));  // open: din
  ROM #(.addrWidth(6), .dataWidth(6)) rom_1 ();  // open: addr, data
  Demultiplexer #(.enable("false"), .width(9)) demultiplexer_1 (
    .out0(demultiplexer_1_out0), .out1(demultiplexer_1_out1), .in(gen_1_dout), .sel(gen_1_ld));
  not not_1 (not_1_out, ram_1_dout_2[0]);
  Register #(.trigger("high"), .width(9)) opand2 (
    .D(demultiplexer_1_out0), .en(not_2_out), .clk(clock_1_out), .Q(opand2_q));  // open: clr
  not not_2 (not_2_out, gen_1_ld);
  gen gen_1 (
    .size(gen_1_size), .dout(gen_1_dout), .ld(gen_1_ld), .addr(ram_1_dout), .clk(clock_1_out),
    .en(ram_1_dout_2[0]), .opcode(ram_1_dout_2[2:1]));
  Register #(.trigger("high"), .width(9)) opand1 (
    .D(demultiplexer_1_out1), .en(gen_1_ld), .clk(clock_1_out), .Q(opand1_q));  // open: clr
  Register #(.trigger("high"), .width(9)) register_1 (
    .D(alu_1_p6), .en(clock_1_out), .clk(clock_1_out), .Q(out_1));  // open: clr
  // alu alu_1: pin names not known; wires that end beside it: opand1_q, opand2_q, gen_1_size, not_1_out, ram_1_dout_2[2:1], alu_1_p6

  // Notes on the sheet:
  //   contents of rom_1 (hex, n*v repeats v):
  //   1 2 4 5 7 3 6
endmodule

module gen (
  input  [8:0] addr,
  input  clk,
  input  [1:0] opcode,
  input  en,
  output [8:0] size,
  output [8:0] dout,
  output ld
);

  wire and_3_out, and_4_out, and_5_out, and_6_out, comparator_1_lt, comparator_2_lt, demultiplexer_1_out0,
       demultiplexer_1_out1, demultiplexer_1_out2, demultiplexer_1_out3, multiplexer_6_out,
       multiplexer_7_out, not_2_out, not_3_out, not_4_out, xor_1_out;
  wire [0:0] bitfinder_1_found;
  wire [2:0] addr_ctr_q;
  wire [3:0] adder_2_out, bitfinder_1_index, index_q;
  wire [5:0] addr_ctr_q_2;
  wire [8:0] adder_1_out, adder_3_out, and_1_out, and_7_out, multiplexer_1_out, multiplexer_2_out,
       multiplexer_3_out, multiplexer_4_out, multiplexer_5_out, not_1_out, nth_q, register_1_q,
       shifter_1_out, shifter_2_out, shifter_3_out, subtractor_1_out, xor_2_out;

  BitFinder #(.\type ("high1"), .width(9)) bitfinder_1 (
    .in(addr), .index(bitfinder_1_index), .found(bitfinder_1_found[0]));
  Adder #(.width(9)) adder_1 (.a(register_1_q), .b(9'h1), .out(adder_1_out));  // open: cin, cout
  Adder #(.width(4)) adder_2 (.a(4'b0001), .b(bitfinder_1_index), .out(adder_2_out));  // open: cin, cout
  Register #(.width(9)) register_1 (
    .D(adder_1_out), .en(1'b1), .clk(clk), .Q(register_1_q), .clr(demultiplexer_1_out2));
  Shifter #(.width(9)) shifter_1 (.in(9'h1), .\dist (adder_2_out), .out(shifter_1_out));
  Demultiplexer #(.enable("false"), .select(2)) demultiplexer_1 (
    .out0(demultiplexer_1_out0), .out1(demultiplexer_1_out1), .out2(demultiplexer_1_out2),
    .out3(demultiplexer_1_out3), .in(1'b1), .sel(opcode));
  assign not_1_out = ~shifter_1_out;  // NOT_Gate not_1, 9 bits wide
  assign and_1_out = not_1_out & {addr[7:0], bitfinder_1_found[0]};  // AND_Gate and_1, 9 bits wide
  Subtractor #(.width(9)) subtractor_1 (.a(shifter_1_out), .b(9'h1), .out(subtractor_1_out));  // open: bin, bout
  not not_2 (not_2_out, clk);
  Adder #(.width(9)) adder_3 (.a({addr_ctr_q_2, addr_ctr_q}), .b(9'h1), .out(adder_3_out));  // open: cin, cout
  Comparator #(.mode("unsigned"), .width(9)) comparator_1 (
    .a(adder_3_out), .b(shifter_1_out), .lt(comparator_1_lt));  // open: gt, eq
  and and_2 (ld, demultiplexer_1_out0, en);
  and and_3 (and_3_out, demultiplexer_1_out1, en);
  and and_4 (and_4_out, demultiplexer_1_out3, en);
  Register #(.width(9)) nth (.D(and_1_out), .en(demultiplexer_1_out2), .clk(not_2_out), .Q(nth_q), .clr(and_3_out));
  Register #(.width(4)) index (
    .D(bitfinder_1_index), .en(demultiplexer_1_out2), .clk(not_2_out), .Q(index_q), .clr(and_3_out));
  Register #(.width(9)) mask (
    .D(subtractor_1_out), .en(demultiplexer_1_out2), .clk(not_2_out), .Q(size), .clr(and_3_out));
  xor xor_1 (xor_1_out, comparator_1_lt, demultiplexer_1_out2);
  and and_5 (and_5_out, clk, xor_1_out);
  Register #(.width(9)) addr_ctr (
    .D(adder_3_out), .en(xor_1_out), .clk(clk), .Q({addr_ctr_q_2, addr_ctr_q}), .clr(demultiplexer_1_out2));
  Shifter #(.shift("lr"), .width(9)) shifter_2 (.in(multiplexer_2_out), .\dist (index_q), .out(shifter_2_out));
  Comparator #(.mode("unsigned"), .width(9)) comparator_2 (
    .a({{5{1'b0}}, index_q}), .b(register_1_q), .lt(comparator_2_lt));  // open: gt, eq
  Shifter #(.width(9)) shifter_3 (.in(multiplexer_2_out), .\dist (4'b0001), .out(shifter_3_out));
  assign xor_2_out = shifter_3_out ^ nth_q;  // XOR_Gate xor_2, 9 bits wide
  and and_6 (and_6_out, shifter_2_out[0], 1'b1);
  Multiplexer #(.enable("false"), .width(9)) multiplexer_1 (
    .in0(shifter_3_out), .in1(xor_2_out), .out(multiplexer_1_out), .sel(and_6_out));
  assign and_7_out = size & multiplexer_1_out;  // AND_Gate and_7, 9 bits wide
  not not_3 (not_3_out, comparator_2_lt);
  Multiplexer #(.enable("false"), .width(9)) multiplexer_2 (
    .in0(nth_q), .in1(dout), .out(multiplexer_2_out), .sel(comparator_2_lt));
  not not_4 (not_4_out, and_5_out);
  Multiplexer #(.enable("false"), .select(3), .width(9)) multiplexer_3 (
    .in0(9'h1), .in1(9'h2), .in2(9'h4), .in3(9'h8), .in4(9'h10), .in5(9'h20), .in6(9'h40), .in7(9'h80),
    .out(multiplexer_3_out), .sel(addr_ctr_q));
  Multiplexer #(.enable("false"), .width(9)) multiplexer_4 (
    .in0(and_7_out), .in1(multiplexer_3_out), .out(multiplexer_4_out), .sel(not_3_out));
  Multiplexer #(.enable("false"), .width(9)) multiplexer_5 (
    .in0(addr), .in1({addr_ctr_q_2, addr_ctr_q}), .out(multiplexer_5_out), .sel(and_4_out));
  Multiplexer #(.enable("false")) multiplexer_6 (.in0(1'b1), .in1(not_4_out), .out(multiplexer_6_out), .sel(and_4_out));
  Multiplexer #(.enable("false")) multiplexer_7 (.in0(clk), .in1(and_5_out), .out(multiplexer_7_out), .sel(and_4_out));
  RAM #(.addrWidth(9), .clearpin("true"), .dataWidth(9)) ram_1 (
    .addr(multiplexer_5_out), .we(and_5_out), .oe(multiplexer_6_out), .clk(multiplexer_7_out),
    .din(multiplexer_4_out), .dout(dout), .clr(and_3_out));

  // Notes on the sheet:
  //   00 - ld
  //   01 - rst
  //   10 - init
  //   11 - gen
  //   rst
  //   gen
endmodule

module pc (
  input  [8:0] size,
  input  clk,
  input  rst,
  input  [2:0] in_4,
  output [8:0] line
);

  wire comparator_1_lt, counter_1_q, demultiplexer_1_out0, demultiplexer_1_out1, demultiplexer_1_out2,
       demultiplexer_1_out3, demultiplexer_1_out4, demultiplexer_1_out7, demultiplexer_2_out0,
       demultiplexer_2_out1, multiplexer_3_out, not_1_out, not_2_out, or_1_out, or_2_out;
  wire [8:0] adder_1_out, multiplexer_1_out, multiplexer_2_out, termctr_q;

  Demultiplexer #(.enable("false"), .select(3)) demultiplexer_1 (
    .out0(demultiplexer_1_out0), .out1(demultiplexer_1_out1), .out2(demultiplexer_1_out2),
    .out3(demultiplexer_1_out3), .out4(demultiplexer_1_out4), .out7(demultiplexer_1_out7), .in(1'b1),
    .sel(in_4));  // open: out5, out6
  Register #(.width(9)) termctr (.D(adder_1_out), .en(not_1_out), .clk(clk), .Q(termctr_q));  // open: clr
  or or_1 (or_1_out, demultiplexer_1_out0, demultiplexer_1_out1, demultiplexer_1_out2, demultiplexer_1_out3, demultiplexer_1_out4);
  or or_2 (or_2_out, clk, or_1_out);
  Comparator #(.mode("unsigned"), .width(9)) comparator_1 (
    .a(size), .b(termctr_q), .lt(comparator_1_lt));  // open: gt, eq
  Multiplexer #(.enable("false"), .width(9)) multiplexer_1 (
    .in0(line), .in1(termctr_q), .out(multiplexer_1_out), .sel(not_1_out));
  Demultiplexer #(.enable("false")) demultiplexer_2 (
    .out0(demultiplexer_2_out0), .out1(demultiplexer_2_out1), .in(or_2_out), .sel(or_1_out));
  Adder #(.width(9)) adder_1 (.a(multiplexer_1_out), .b(9'h1), .out(adder_1_out));  // open: cin, cout
  not not_1 (not_1_out, comparator_1_lt);
  Multiplexer #(.enable("false"), .width(9)) multiplexer_2 (
    .in0(adder_1_out), .in1(line), .out(multiplexer_2_out), .sel(not_1_out));
  Counter #(.max('h1), .width(1)) counter_1 (
    .count(demultiplexer_2_out1), .Q(counter_1_q), .up(1'b1), .clk(clk));  // open: load, D, carry, clr
  Register #(.width(9)) pcctr (.D(multiplexer_2_out), .en(1'b1), .clk(not_2_out), .Q(line), .clr(rst));
  not not_2 (not_2_out, multiplexer_3_out);
  Multiplexer #(.enable("false")) multiplexer_3 (
    .in0(demultiplexer_2_out0), .in1(counter_1_q), .out(multiplexer_3_out), .sel(or_1_out));
endmodule

module cu (
  input  [1:0] in_1
);

  Multiplexer #(.enable("false"), .select(2), .width(9)) multiplexer_1 (.sel(in_1));  // open: in0, in1, in2, in3, out
endmodule
