// Logisim project divu.circ as structural Verilog: 1 circuit, main circuit div
module div (
  input  [3:0] in_1,
  input  [3:0] in_2,
  output [3:0] out_3
);

  wire comparator_1_gt, comparator_1_lt;
  wire [3:0] multiplexer_1_out, multiplexer_2_out, subtractor_1_out;

  Multiplexer #(.enable("false"), .width(4)) multiplexer_1 (
    .in0(in_2), .in1(in_1), .out(multiplexer_1_out), .sel(comparator_1_gt));
  Comparator #(.mode("unsigned"), .width(4)) comparator_1 (
    .a(in_1), .b(in_2), .gt(comparator_1_gt), .lt(comparator_1_lt));  // open: eq
  Multiplexer #(.enable("false"), .width(4)) multiplexer_2 (
    .in0(in_2), .in1(in_1), .out(multiplexer_2_out), .sel(comparator_1_lt));
  Subtractor #(.width(4)) subtractor_1 (
    .a(multiplexer_1_out), .b(multiplexer_2_out), .out(subtractor_1_out));  // open: bin, bout
  assign out_3 = subtractor_1_out & 4'b0111;  // AND_Gate and_1, 4 bits wide
endmodule
