// Logisim project mul.circ as structural Verilog: 1 circuit, main circuit mul
module mul (
  input  [8:0] opand1,
  input  [8:0] opand2,
  input  [8:0] size,
  output [8:0] result
);

  wire [8:0] adder_1_out;

  Adder #(.width(9)) adder_1 (.a(opand1), .b(opand2), .out(adder_1_out));  // open: cin, cout
  Divider #(.width(9)) divider_1 (.a(adder_1_out), .b(size), .rem(result));  // open: out, upper
endmodule
